# Fritzing sketch extended wiring diagram (saved by Fritzing 0.9.3b)
breadboards: 1

parts:
  Arduino_Uno = Arduino Uno (Rev3)
  WeMos_D1_Mini2 = WeMos D1 Mini
  Mod1 = KY-018 Photoresistor Module [package="Breakout board"]
  LED1 = LED - 5mm [color="Red (633nm)" package="5 mm [THT]"]
  VCC1 = Battery block 9V
  R1 = Resistor [tolerance=±5% resistance=470 package="0603 [SMD]"]
  Mod2 = KY-018 Photoresistor Module [package="Breakout board"]
  LED2 = LED - 5mm [color="Red (633nm)" package="5 mm [THT]"]
  VCC2 = Battery block 9V
  R2 = Resistor [tolerance=±5% resistance=470 package="0603 [SMD]"]
  Mod3 = KY-018 Photoresistor Module [package="Breakout board"]
  LED3 = LED - 5mm [color="Red (633nm)" package="5 mm [THT]"]
  VCC3 = Battery block 9V
  R3 = Resistor [tolerance=±5% resistance=470 package="0603 [SMD]"]
  SP1 = SPEAKER [package=pcb_mount_speaker]
  S2 = Round Pushbutton
  S3 = Round Pushbutton

nets:
  N1: Arduino_Uno.A0, Mod1.S, Mod2.S, Mod3.S
  N2: Arduino_Uno.D9_PWM, SP1.-
  N3: Arduino_Uno.D11_PWM/MOSI, S3.leg0
  N4: Arduino_Uno.D12/MISO, S2.leg0
  N5: Arduino_Uno.GND, WeMos_D1_Mini2.G, Mod1.-, Mod2.-, Mod3.-, SP1.+, S2.leg1, S3.leg1
  N6: Arduino_Uno.D0/RX, WeMos_D1_Mini2.TX
  N7: Arduino_Uno.D1/TX, WeMos_D1_Mini2.RX
  VIN: Arduino_Uno.5V, WeMos_D1_Mini2.5V, Mod1.Vin, Mod2.Vin, Mod3.Vin
  N8: LED1.cathode, VCC1.-
  N9: LED1.anode, R1.Pin_0
  N10: VCC1.+, R1.Pin_1
  N11: LED2.cathode, VCC2.-
  N12: LED2.anode, R2.Pin_0
  N13: VCC2.+, R2.Pin_1
  N14: LED3.cathode, VCC3.-
  N15: LED3.anode, R3.Pin_0
  N16: VCC3.+, R3.Pin_1

custom parts:
  KY-018 Photoresistor Module: KY-018 Photoresistor module, used to measure light intensity. It can determine the presence or absence of light.
