# Fritzing sketch wiring diagram 3.0 (saved by Fritzing 0.9.3b)
breadboards: 1

parts:
  Arduino_Uno = Arduino Uno (Rev3)
  WeMos_D1_Mini2 = WeMos D1 Mini
  photodiod_1 = KY-018 Photoresistor Module [package="Breakout board"]
  Laser1 = LED - 5mm [color="Red (633nm)" package="5 mm [THT]"]
  VCC1 = Battery block 9V
  R1 = Resistor [tolerance=±5% resistance=470 package="0603 [SMD]"]
  photodiod_2 = KY-018 Photoresistor Module [package="Breakout board"]
  Laser2 = LED - 5mm [color="Red (633nm)" package="5 mm [THT]"]
  VCC2 = Battery block 9V
  R2 = Resistor [tolerance=±5% resistance=470 package="0603 [SMD]"]
  photodiod_3 = KY-018 Photoresistor Module [package="Breakout board"]
  Laser3 = LED - 5mm [color="Red (633nm)" package="5 mm [THT]"]
  VCC3 = Battery block 9V
  R3 = Resistor [tolerance=±5% resistance=470 package="0603 [SMD]"]
  SP1 = SPEAKER [package=pcb_mount_speaker]
  start_button = Round Pushbutton
  stop_button = Round Pushbutton
  LED1 = LED - 5mm [color="Red (633nm)" package="5 mm [THT]"]
  R4 = Resistor [tolerance=±5% resistance=220 package=THT]
  LED2 = LED - 5mm [color="Red (633nm)" package="5 mm [THT]"]
  R5 = Resistor [tolerance=±5% resistance=220 package=THT]
  LED3 = LED - 5mm [color="Red (633nm)" package="5 mm [THT]"]
  R6 = Resistor [tolerance=±5% resistance=220 package=THT]
  D1 = Rectifier Diode [part_number=1N4001 package="300 mil [THT]"]
  D2 = Rectifier Diode [part_number=1N4001 package="300 mil [THT]"]
  D3 = Rectifier Diode [part_number=1N4001 package="300 mil [THT]"]
  RGB-LED = RGB LED (com. cathode, rgb) [package="5 mm [THT]"]
  LED4 = LED - 5mm [color="Red (633nm)" package="5 mm [THT]"]  # not connected
  LED5 = Red LED - 5mm [package="5 mm [THT]"]

nets:
  N1: Arduino_Uno.A0, photodiod_1.S, photodiod_2.S, photodiod_3.S, LED1.anode, LED2.anode, LED3.anode
  N2: Arduino_Uno.D9_PWM, SP1.-
  N3: Arduino_Uno.D11_PWM/MOSI, stop_button.leg0
  N4: Arduino_Uno.D12/MISO, start_button.leg0
  N5: Arduino_Uno.GND, WeMos_D1_Mini2.G, photodiod_1.-, photodiod_2.-, photodiod_3.-, SP1.+, start_button.leg1, stop_button.leg1, D1.cathode, D2.cathode, D3.cathode, RGB-LED.common_cathode
  N6: Arduino_Uno.D0/RX, WeMos_D1_Mini2.TX
  N7: Arduino_Uno.D1/TX, WeMos_D1_Mini2.RX
  VIN: Arduino_Uno.5V, WeMos_D1_Mini2.5V, photodiod_1.Vin, photodiod_2.Vin, photodiod_3.Vin
  N8: WeMos_D1_Mini2.D0, RGB-LED.blue_anode
  N9: WeMos_D1_Mini2.D5, RGB-LED.green_anode
  N10: WeMos_D1_Mini2.D6, RGB-LED.red_anode
  N11: Laser1.cathode, VCC1.-
  N12: Laser1.anode, R1.Pin_0, LED5.anode
  N13: VCC1.+, R1.Pin_1
  N14: Laser2.cathode, VCC2.-
  N15: Laser2.anode, R2.Pin_0
  N16: VCC2.+, R2.Pin_1
  N17: Laser3.cathode, VCC3.-
  N18: Laser3.anode, R3.Pin_0
  N19: VCC3.+, R3.Pin_1
  N20: LED1.cathode, R4.Pin_1
  N21: R4.Pin_0, D1.anode
  N22: LED2.cathode, R5.Pin_1
  N23: R5.Pin_0, D2.anode
  N24: LED3.cathode, R6.Pin_1
  N25: R6.Pin_0, D3.anode

custom parts:
  KY-018 Photoresistor Module: KY-018 Photoresistor module, used to measure light intensity. It can determine the presence or absence of light.
  Red LED - 5mm: A generic red LED (~1.8V)
