# Fritzing sketch wiring diagram_2.1.1 (saved by Fritzing 0.9.3b)
breadboards: 1

parts:
  photodiod_1 = KY-018 Photoresistor Module [package="Breakout board"]
  photodiod_2 = KY-018 Photoresistor Module [package="Breakout board"]
  start_button = Momentary Switch [package=ksa_sealed_tac_switch]
  stop_button = Momentary Switch [package=ksa_sealed_tac_switch]
  Bauteil1 = Arduino Uno (Rev3)
  speaker = SPEAKER [package=pcb_mount_speaker]

nets:
  N1: photodiod_1.S, Bauteil1.A0
  VIN: photodiod_1.Vin, photodiod_2.Vin, Bauteil1.5V
  N2: photodiod_1.-, photodiod_2.-, start_button.4, stop_button.4, Bauteil1.GND, speaker.+
  N3: photodiod_2.S, Bauteil1.A1
  N4: start_button.1, Bauteil1.D12/MISO
  N5: stop_button.1, Bauteil1.D11_PWM/MOSI
  N6: Bauteil1.D9_PWM, speaker.-

custom parts:
  KY-018 Photoresistor Module: KY-018 Photoresistor module, used to measure light intensity. It can determine the presence or absence of light.
